# Fritzing sketch S102 (saved by Fritzing 0.9.2b)
breadboards: 1

parts:
  Raspberry_Pi_B_rev1 = Raspberry Pi B rev1
  7_Segment1 = 7 Segment Display
  7_Segment2 = 7 Segment Display
  7_Segment3 = 7 Segment Display
  7_Segment4 = 7 Segment Display
  U1 = GPS-09838 [package=ls20126]

nets:
  3V3: Raspberry_Pi_B_rev1.3V3, U1.VCC
  N1: Raspberry_Pi_B_rev1.GPIO_1, 7_Segment3.Segment_G, 7_Segment3.Segment_F
  N2: Raspberry_Pi_B_rev1.GND, U1.GPIO
  N3: Raspberry_Pi_B_rev1.GPIO_14, U1.EN
  N4: Raspberry_Pi_B_rev1.GPIO_15, U1.BOOTSL
  N5: Raspberry_Pi_B_rev1.GPIO_21, 7_Segment3.Segment_D
  N6: Raspberry_Pi_B_rev1.GPIO_4, 7_Segment2.Segment_DP
  N7: Raspberry_Pi_B_rev1.GPIO_24, 7_Segment2.Segment_B, 7_Segment2.Segment_A
  N8: 7_Segment1.Segment_G, 7_Segment1.Segment_F
  N9: 7_Segment1.Segment_B, 7_Segment1.Segment_A
  N10: 7_Segment2.Segment_G, 7_Segment2.Segment_F
  N11: 7_Segment3.Segment_B, 7_Segment3.Segment_A
  N12: 7_Segment4.Segment_G, 7_Segment4.Segment_F
  N13: 7_Segment4.Segment_B, 7_Segment4.Segment_A
